// Logisim project ALU_with_controls.circ as structural Verilog: 1 circuit, main circuit ALU_with_controls
module ALU_with_controls (
  input  in_1,
  input  in_2,
  input  in_3,
  input  in_4,
  input  in_5,
  input  in_6,
  input  in_7,
  input  in_8,
  input  in_9,
  input  in_10,
  input  in_11,
  input  in_12,
  input  [1:0] in_13,
  output out_14,
  output out_15,
  output out_16,
  output out_17,
  output out_18,
  output out_19,
  output out_20,
  output out_21
);

  wire and_1_out, and_2_out, and_3_out, controlled_buffer_1_out, controlled_buffer_3_out,
       controlled_buffer_5_out, controlled_buffer_6_out, controlled_buffer_7_out, controlled_buffer_11_out,
       controlled_buffer_12_out, d_ff_1_q, d_ff_2_q, d_ff_3_q, d_ff_3_qn, d_ff_4_q, d_ff_4_qn,
       general_purpose_register_1_p5, general_purpose_register_1_p7, general_purpose_register_1_p9,
       general_purpose_register_1_p11, not_1_out, not_2_out, not_4_out, or_1_out;

  // General_Purpose_Register general_purpose_register_1: pin names not known; wires that end beside it: in_10, in_11, 1'b1, in_6, general_purpose_register_1_p5, in_7, general_purpose_register_1_p7, in_8, general_purpose_register_1_p9, in_9, general_purpose_register_1_p11
  and and_1 (and_1_out, in_13[0], in_13[1]);
  and and_2 (and_2_out, in_11, and_1_out, or_1_out);
  not not_1 (not_1_out, in_5);
  assign controlled_buffer_1_out = in_5 ? in_1 : 1'bz;  // Controlled_Buffer controlled_buffer_1
  assign controlled_buffer_1_out = not_1_out ? d_ff_1_q : 1'bz;  // Controlled_Buffer controlled_buffer_2
  ALU_design1 alu_design1_1 (
    .in_9(in_12), .in_10(in_13), .in_11(and_2_out), .out_12(out_15), .in_1(general_purpose_register_1_p5),
    .in_2(general_purpose_register_1_p7), .in_3(general_purpose_register_1_p9),
    .in_4(general_purpose_register_1_p11), .in_5(d_ff_1_q), .in_6(d_ff_2_q), .in_7(d_ff_3_q),
    .in_8(d_ff_4_q), .out_15(out_18), .out_16(out_19), .out_17(out_20), .out_18(out_21), .out_13(out_16),
    .out_14(out_17));
  D_Flip_Flop d_ff_1 (.clk(in_11), .D(controlled_buffer_1_out), .Q(d_ff_1_q));  // open: Qn, preset, en, reset
  assign controlled_buffer_3_out = in_5 ? in_2 : 1'bz;  // Controlled_Buffer controlled_buffer_3
  assign controlled_buffer_3_out = not_1_out ? d_ff_2_q : 1'bz;  // Controlled_Buffer controlled_buffer_4
  D_Flip_Flop d_ff_2 (.clk(in_11), .D(controlled_buffer_3_out), .Q(d_ff_2_q));  // open: Qn, preset, en, reset
  not not_2 (not_2_out, and_3_out);
  assign controlled_buffer_5_out = not_2_out ? in_11 : 1'bz;  // Controlled_Buffer controlled_buffer_5
  assign controlled_buffer_6_out = in_5 ? in_3 : 1'bz;  // Controlled_Buffer controlled_buffer_6
  or or_1 (or_1_out, d_ff_4_q, d_ff_3_q);
  assign controlled_buffer_7_out = not_4_out ? d_ff_3_q : 1'bz;  // Controlled_Buffer controlled_buffer_7
  assign controlled_buffer_6_out = not_1_out ? controlled_buffer_7_out : 1'bz;  // Controlled_Buffer controlled_buffer_8
  D_Flip_Flop d_ff_3 (
    .clk(controlled_buffer_5_out), .D(controlled_buffer_6_out), .Q(d_ff_3_q), .Qn(d_ff_3_qn));  // open: preset, en, reset
  assign controlled_buffer_6_out = and_3_out ? d_ff_3_qn : 1'bz;  // Controlled_Buffer controlled_buffer_9
  assign controlled_buffer_5_out = and_3_out ? d_ff_4_q : 1'bz;  // Controlled_Buffer controlled_buffer_10
  assign controlled_buffer_11_out = in_5 ? in_4 : 1'bz;  // Controlled_Buffer controlled_buffer_11
  assign controlled_buffer_12_out = not_4_out ? d_ff_4_q : 1'bz;  // Controlled_Buffer controlled_buffer_12
  assign controlled_buffer_11_out = not_1_out ? controlled_buffer_12_out : 1'bz;  // Controlled_Buffer controlled_buffer_13
  D_Flip_Flop d_ff_4 (
    .clk(in_11), .D(controlled_buffer_11_out), .Q(d_ff_4_q), .Qn(d_ff_4_qn));  // open: preset, en, reset
  assign controlled_buffer_11_out = and_3_out ? d_ff_4_qn : 1'bz;  // Controlled_Buffer controlled_buffer_14
  not not_3 (out_14, or_1_out);
  not not_4 (not_4_out, and_3_out);
  and and_3 (and_3_out, and_1_out, not_1_out, or_1_out);
endmodule
