// Logisim project Architecture.circ as structural Verilog: 1 circuit, main circuit Architecture1
module Architecture1 (
);

  wire alu_with_controls_1_p13, alu_with_controls_1_p14, alu_with_controls_1_p16, alu_with_controls_1_p18,
       alu_with_controls_1_p19, alu_with_controls_1_p20, alu_with_controls_1_p21, clock_1_out,
       instruction_register_1_p9, instruction_register_1_p10, instruction_register_1_p11,
       instruction_register_1_p12, instruction_register_1_p13, instruction_register_1_p14,
       instruction_register_1_p15, instruction_register_1_p16, instruction_register_1_p17,
       instruction_register_1_p18, instruction_register_1_p20, or_1_out, program_counter_1_p1,
       program_counter_1_p5, program_counter_1_p9, program_counter_1_p12, program_counter_1_p13,
       program_counter_1_p14, program_counter_1_p15, pull_resistor_7_node, R1_p1, R1_p3, R1_p5, R1_p10,
       R1_p13, R1_p15, R2_p1, R2_p3, R2_p5, R2_p10, R2_p13, R2_p15, R3_p1, R3_p3, R3_p5, R3_p10, R3_p13,
       R3_p15, R4_p1, R4_p3, R4_p5, R4_p10, R4_p13, R4_p15, ram_rom_with_mar_1_p1, ram_rom_with_mar_1_p3,
       ram_rom_with_mar_1_p4, ram_rom_with_mar_1_p5, ram_rom_with_mar_1_p6, Status_Register_p5,
       Status_Register_p7, Status_Register_p9, Status_Register_p11;
  wire [1:0] alu_with_controls_1_p17;
  wire [3:0] R1_p12;

  Clock clock_1 (.out(clock_1_out));
  // General_Purpose_Register R1: pin names not known; wires that end beside it: R1_p1, clock_1_out, R1_p3, R1_p12[3], R1_p5, R1_p12[3], R1_p12[2], R1_p12[2], R1_p12[1], R1_p10, R1_p12[1], R1_p12[0], R1_p13, R1_p12[0], R1_p15
  LED led_1 (.in(R1_p5));
  // General_Purpose_Register R3: pin names not known; wires that end beside it: R3_p1, clock_1_out, R3_p3, R1_p12[3], R3_p5, R1_p12[3], R1_p12[2], R1_p12[2], R1_p12[1], R3_p10, R1_p12[1], R1_p12[0], R3_p13, R1_p12[0], R3_p15
  LED led_2 (.in(R3_p5));
  LED led_3 (.in(R1_p10));
  LED led_4 (.in(R1_p15));
  LED led_5 (.in(R1_p13));
  LED led_6 (.in(R3_p15));
  LED led_7 (.in(R3_p10));
  LED led_8 (.in(R3_p13));
  // General_Purpose_Register R2: pin names not known; wires that end beside it: R2_p1, clock_1_out, R2_p3, R1_p12[3], R2_p5, R1_p12[3], R1_p12[2], R1_p12[2], R1_p12[1], R2_p10, R1_p12[1], R1_p12[0], R2_p13, R1_p12[0], R2_p15
  // General_Purpose_Register R4: pin names not known; wires that end beside it: R4_p1, clock_1_out, R4_p3, R1_p12[3], R4_p5, R1_p12[3], R1_p12[2], R1_p12[2], R1_p12[1], R4_p10, R1_p12[1], R1_p12[0], R4_p13, R1_p12[0], R4_p15
  LED led_9 (.in(R2_p13));
  LED led_10 (.in(R2_p5));
  LED led_11 (.in(R2_p10));
  LED led_12 (.in(R4_p13));
  LED led_13 (.in(R4_p10));
  LED led_14 (.in(R4_p5));
  LED led_15 (.in(R2_p15));
  LED led_16 (.in(R4_p15));
  // RAM_ROM_with_MAR ram_rom_with_mar_1: pin names not known; wires that end beside it: ram_rom_with_mar_1_p1, clock_1_out, ram_rom_with_mar_1_p3, ram_rom_with_mar_1_p4, ram_rom_with_mar_1_p5, ram_rom_with_mar_1_p6, R1_p12, R1_p12, R1_p12[0], R1_p12[1], R1_p12[2], R1_p12[3]
  LED led_17 (.in(R1_p12[2]));
  LED led_18 (.in(R1_p12[3]));
  Pull_Resistor pull_resistor_1 (.node(R1_p12[3]));
  Pull_Resistor pull_resistor_2 (.node(R1_p12[2]));
  LED led_19 (.in(R1_p12[1]));
  LED led_20 (.in(R1_p12[0]));
  Pull_Resistor pull_resistor_3 (.node(R1_p12[1]));
  Pull_Resistor pull_resistor_4 (.node(R1_p12[0]));
  // Program_counter program_counter_1: pin names not known; wires that end beside it: program_counter_1_p1, R1_p12[3], R1_p12[3], R1_p12[2], program_counter_1_p5, R1_p12[2], R1_p12[1], R1_p12[1], program_counter_1_p9, R1_p12[0], R1_p12[0], program_counter_1_p12, program_counter_1_p13, program_counter_1_p14, program_counter_1_p15, clock_1_out
  LED led_21 (.in(program_counter_1_p1));
  LED led_22 (.in(program_counter_1_p5));
  LED led_23 (.in(instruction_register_1_p9));
  LED led_24 (.in(program_counter_1_p12));
  LED led_25 (.in(program_counter_1_p9));
  // ALU_with_controls alu_with_controls_1: pin names not known; wires that end beside it: R1_p12[3], R1_p12[2], R1_p12[1], R1_p12[0], R1_p12[3], R1_p12[2], R1_p12[1], R1_p12[3], R1_p12[0], R1_p12[2], R1_p12[1], R1_p12[0], alu_with_controls_1_p13, alu_with_controls_1_p14, clock_1_out, alu_with_controls_1_p16, alu_with_controls_1_p17, alu_with_controls_1_p18, alu_with_controls_1_p19, alu_with_controls_1_p20, alu_with_controls_1_p21
  // Instruction_Register instruction_register_1: pin names not known; wires that end beside it: R1_p12[3], R1_p12[2], R1_p12[1], R1_p12[0], R1_p12[3], R1_p12[2], R1_p12[1], R1_p12[0], instruction_register_1_p9, instruction_register_1_p10, instruction_register_1_p11, instruction_register_1_p12, instruction_register_1_p13, instruction_register_1_p14, instruction_register_1_p15, instruction_register_1_p16, instruction_register_1_p17, instruction_register_1_p18, clock_1_out, instruction_register_1_p20
  LED led_26 (.in(instruction_register_1_p12));
  LED led_27 (.in(instruction_register_1_p10));
  LED led_28 (.in(instruction_register_1_p13));
  LED led_29 (.in(instruction_register_1_p11));
  LED led_30 (.in(instruction_register_1_p16));
  LED led_31 (.in(instruction_register_1_p14));
  LED led_32 (.in(instruction_register_1_p15));
  Control_logic_main main_1 (
    .in_9(clock_1_out), .in_10(alu_with_controls_1_p18), .in_11(Status_Register_p5),
    .in_12(Status_Register_p7), .in_13(Status_Register_p9), .in_1(instruction_register_1_p9),
    .in_2(instruction_register_1_p10), .in_3(instruction_register_1_p11), .in_4(instruction_register_1_p12),
    .in_5(instruction_register_1_p13), .in_6(instruction_register_1_p14), .in_7(instruction_register_1_p15),
    .in_8(instruction_register_1_p16), .MARin(ram_rom_with_mar_1_p1), .out_34(ram_rom_with_mar_1_p3),
    .RAMData(ram_rom_with_mar_1_p4), .out_36(ram_rom_with_mar_1_p5), .ROM2out(ram_rom_with_mar_1_p6),
    .R1in(R1_p1), .out_15(R1_p3), .R2in(R2_p1), .out_17(R2_p3), .R3in(R3_p1), .R3out(R3_p3), .out_20(R4_p1),
    .R4out(R4_p3), .out_22(program_counter_1_p13), .PCClkEN(program_counter_1_p14),
    .PCout(program_counter_1_p15), .out_25(alu_with_controls_1_p13), .Yin(alu_with_controls_1_p14),
    .out_27(alu_with_controls_1_p16), .MSBin(instruction_register_1_p17), .LSBin(instruction_register_1_p18),
    .out_30(instruction_register_1_p20), .DO1(alu_with_controls_1_p17[1]), .out_32(alu_with_controls_1_p17[0]));
  LED led_33 (.in(alu_with_controls_1_p19));
  LED led_34 (.in(alu_with_controls_1_p20));
  LED led_35 (.in(alu_with_controls_1_p21));
  LED led_36 (.in(alu_with_controls_1_p18));
  or or_1 (or_1_out, alu_with_controls_1_p17[0], alu_with_controls_1_p17[1]);
  Pull_Resistor pull_resistor_5 (.node(alu_with_controls_1_p21));
  Pull_Resistor pull_resistor_6 (.node(alu_with_controls_1_p19));
  Pull_Resistor pull_resistor_7 (.node(pull_resistor_7_node));
  // General_Purpose_Register Status_Register: pin names not known; wires that end beside it: or_1_out, clock_1_out, 1'b1, alu_with_controls_1_p21, Status_Register_p5, alu_with_controls_1_p20, Status_Register_p7, alu_with_controls_1_p19, Status_Register_p9, pull_resistor_7_node, Status_Register_p11
  LED led_37 (.in(Status_Register_p7));
  LED led_38 (.in(Status_Register_p9));
  LED led_39 (.in(Status_Register_p5));
  LED led_40 (.in(Status_Register_p11));

  // Notes on the sheet:
  //   R1
  //   R3
  //   R2
  //   R4
  //   Status Register
  //   N
  //   Z
  //   C
endmodule
