// Logisim project CPU_Architecture.circ as structural Verilog: 1 circuit, main circuit Architecture1
module Architecture1 (
  input  A3_in,
  input  A2_in,
  input  A1_in,
  input  A0_in,
  input  Clk,
  output A3_out,
  output A2_out,
  output A1_out,
  output A0_out,
  output MARin,
  output RAM_EN,
  output Data_in_bar___Data_out,
  output ROM1_out,
  output ROM2_out
);

  wire alu_with_controls_1_p13, alu_with_controls_1_p14, alu_with_controls_1_p16, alu_with_controls_1_p18,
       alu_with_controls_1_p19, alu_with_controls_1_p20, alu_with_controls_1_p21, controlled_buffer_1_out,
       controlled_buffer_2_out, controlled_buffer_3_out, controlled_buffer_4_out, instruction_register_1_p9,
       instruction_register_1_p10, instruction_register_1_p11, instruction_register_1_p12,
       instruction_register_1_p13, instruction_register_1_p14, instruction_register_1_p15,
       instruction_register_1_p16, instruction_register_1_p17, instruction_register_1_p18,
       instruction_register_1_p20, or_1_out, or_2_out, or_3_out, program_counter_1_p1, program_counter_1_p5,
       program_counter_1_p9, program_counter_1_p12, program_counter_1_p13, program_counter_1_p14,
       program_counter_1_p15, pull_resistor_7_node, R1_p1, R1_p3, R1_p5, R1_p10, R1_p13, R1_p15, R2_p1,
       R2_p3, R2_p5, R2_p10, R2_p13, R2_p15, R3_p1, R3_p3, R3_p5, R3_p10, R3_p13, R3_p15, R4_p1, R4_p3,
       R4_p5, R4_p10, R4_p13, R4_p15, Status_Register_p5, Status_Register_p7, Status_Register_p9,
       Status_Register_p11;
  wire [1:0] alu_with_controls_1_p17;

  assign controlled_buffer_1_out = or_1_out ? A3_in : 1'bz;  // Controlled_Buffer controlled_buffer_1
  assign controlled_buffer_2_out = or_1_out ? A2_in : 1'bz;  // Controlled_Buffer controlled_buffer_2
  assign controlled_buffer_3_out = or_1_out ? A1_in : 1'bz;  // Controlled_Buffer controlled_buffer_3
  assign controlled_buffer_4_out = or_1_out ? A0_in : 1'bz;  // Controlled_Buffer controlled_buffer_4
  or or_1 (or_1_out, ROM2_out, ROM1_out, RAM_EN);
  // General_Purpose_Register R1: pin names not known; wires that end beside it: R1_p1, Clk, R1_p3, controlled_buffer_1_out, R1_p5, controlled_buffer_1_out, controlled_buffer_2_out, controlled_buffer_2_out, controlled_buffer_3_out, R1_p10, controlled_buffer_3_out, controlled_buffer_4_out, R1_p13, controlled_buffer_4_out, R1_p15
  LED led_1 (.in(R1_p5));
  // General_Purpose_Register R3: pin names not known; wires that end beside it: R3_p1, Clk, R3_p3, controlled_buffer_1_out, R3_p5, controlled_buffer_1_out, controlled_buffer_2_out, controlled_buffer_2_out, controlled_buffer_3_out, R3_p10, controlled_buffer_3_out, controlled_buffer_4_out, R3_p13, controlled_buffer_4_out, R3_p15
  LED led_2 (.in(R3_p5));
  LED led_3 (.in(R1_p13));
  LED led_4 (.in(R1_p15));
  LED led_5 (.in(R1_p10));
  LED led_6 (.in(R3_p15));
  LED led_7 (.in(R3_p10));
  LED led_8 (.in(R3_p13));
  // General_Purpose_Register R2: pin names not known; wires that end beside it: R2_p1, Clk, R2_p3, controlled_buffer_1_out, R2_p5, controlled_buffer_1_out, controlled_buffer_2_out, controlled_buffer_2_out, controlled_buffer_3_out, R2_p10, controlled_buffer_3_out, controlled_buffer_4_out, R2_p13, controlled_buffer_4_out, R2_p15
  // General_Purpose_Register R4: pin names not known; wires that end beside it: R4_p1, Clk, R4_p3, controlled_buffer_1_out, R4_p5, controlled_buffer_1_out, controlled_buffer_2_out, controlled_buffer_2_out, controlled_buffer_3_out, R4_p10, controlled_buffer_3_out, controlled_buffer_4_out, R4_p13, controlled_buffer_4_out, R4_p15
  or or_2 (or_2_out, MARin, Data_in_bar___Data_out);
  LED led_9 (.in(R2_p10));
  LED led_10 (.in(R2_p5));
  LED led_11 (.in(R2_p13));
  LED led_12 (.in(R4_p10));
  LED led_13 (.in(R4_p5));
  LED led_14 (.in(R4_p13));
  LED led_15 (.in(R2_p15));
  LED led_16 (.in(R4_p15));
  assign A3_out = or_2_out ? controlled_buffer_1_out : 1'bz;  // Controlled_Buffer controlled_buffer_5
  assign A2_out = or_2_out ? controlled_buffer_2_out : 1'bz;  // Controlled_Buffer controlled_buffer_6
  assign A1_out = or_2_out ? controlled_buffer_3_out : 1'bz;  // Controlled_Buffer controlled_buffer_7
  assign A0_out = or_2_out ? controlled_buffer_4_out : 1'bz;  // Controlled_Buffer controlled_buffer_8
  LED led_17 (.in(controlled_buffer_2_out));
  LED led_18 (.in(controlled_buffer_1_out));
  Pull_Resistor pull_resistor_1 (.node(controlled_buffer_2_out));
  Pull_Resistor pull_resistor_2 (.node(controlled_buffer_1_out));
  LED led_19 (.in(controlled_buffer_4_out));
  LED led_20 (.in(controlled_buffer_3_out));
  Pull_Resistor pull_resistor_3 (.node(controlled_buffer_4_out));
  Pull_Resistor pull_resistor_4 (.node(controlled_buffer_3_out));
  // Program_counter program_counter_1: pin names not known; wires that end beside it: program_counter_1_p1, controlled_buffer_1_out, controlled_buffer_1_out, controlled_buffer_2_out, program_counter_1_p5, controlled_buffer_2_out, controlled_buffer_3_out, controlled_buffer_3_out, program_counter_1_p9, controlled_buffer_4_out, controlled_buffer_4_out, program_counter_1_p12, program_counter_1_p13, program_counter_1_p14, program_counter_1_p15, Clk
  LED led_21 (.in(program_counter_1_p5));
  LED led_22 (.in(program_counter_1_p1));
  LED led_23 (.in(instruction_register_1_p9));
  LED led_24 (.in(program_counter_1_p9));
  LED led_25 (.in(program_counter_1_p12));
  // ALU_with_controls alu_with_controls_1: pin names not known; wires that end beside it: controlled_buffer_1_out, controlled_buffer_2_out, controlled_buffer_3_out, controlled_buffer_4_out, controlled_buffer_1_out, controlled_buffer_2_out, controlled_buffer_3_out, controlled_buffer_1_out, controlled_buffer_4_out, controlled_buffer_2_out, controlled_buffer_3_out, controlled_buffer_4_out, alu_with_controls_1_p13, alu_with_controls_1_p14, Clk, alu_with_controls_1_p16, alu_with_controls_1_p17, alu_with_controls_1_p18, alu_with_controls_1_p19, alu_with_controls_1_p20, alu_with_controls_1_p21
  // Instruction_Register instruction_register_1: pin names not known; wires that end beside it: controlled_buffer_1_out, controlled_buffer_2_out, controlled_buffer_3_out, controlled_buffer_4_out, controlled_buffer_1_out, controlled_buffer_2_out, controlled_buffer_3_out, controlled_buffer_4_out, instruction_register_1_p9, instruction_register_1_p10, instruction_register_1_p11, instruction_register_1_p12, instruction_register_1_p13, instruction_register_1_p14, instruction_register_1_p15, instruction_register_1_p16, instruction_register_1_p17, instruction_register_1_p18, Clk, instruction_register_1_p20
  LED led_26 (.in(instruction_register_1_p10));
  LED led_27 (.in(instruction_register_1_p11));
  LED led_28 (.in(instruction_register_1_p12));
  LED led_29 (.in(instruction_register_1_p13));
  LED led_30 (.in(instruction_register_1_p14));
  LED led_31 (.in(instruction_register_1_p16));
  LED led_32 (.in(instruction_register_1_p15));
  Control_logic_main main_1 (
    .in_9(Clk), .in_10(alu_with_controls_1_p18), .in_11(Status_Register_p5), .in_12(Status_Register_p7),
    .in_13(Status_Register_p9), .in_1(instruction_register_1_p9), .in_2(instruction_register_1_p10),
    .in_3(instruction_register_1_p11), .in_4(instruction_register_1_p12), .in_5(instruction_register_1_p13),
    .in_6(instruction_register_1_p14), .in_7(instruction_register_1_p15), .in_8(instruction_register_1_p16),
    .MARin(MARin), .out_34(RAM_EN), .RAMData(Data_in_bar___Data_out), .out_36(ROM1_out), .ROM2out(ROM2_out),
    .R1in(R1_p1), .out_15(R1_p3), .R2in(R2_p1), .out_17(R2_p3), .R3in(R3_p1), .R3out(R3_p3), .out_20(R4_p1),
    .R4out(R4_p3), .out_22(program_counter_1_p13), .PCClkEN(program_counter_1_p14),
    .PCout(program_counter_1_p15), .out_25(alu_with_controls_1_p13), .Yin(alu_with_controls_1_p14),
    .out_27(alu_with_controls_1_p16), .MSBin(instruction_register_1_p17), .LSBin(instruction_register_1_p18),
    .out_30(instruction_register_1_p20), .DO1(alu_with_controls_1_p17[1]), .out_32(alu_with_controls_1_p17[0]));
  LED led_33 (.in(alu_with_controls_1_p19));
  LED led_34 (.in(alu_with_controls_1_p20));
  LED led_35 (.in(alu_with_controls_1_p21));
  LED led_36 (.in(alu_with_controls_1_p18));
  or or_3 (or_3_out, alu_with_controls_1_p17[0], alu_with_controls_1_p17[1]);
  Pull_Resistor pull_resistor_5 (.node(alu_with_controls_1_p21));
  Pull_Resistor pull_resistor_6 (.node(alu_with_controls_1_p19));
  Pull_Resistor pull_resistor_7 (.node(pull_resistor_7_node));
  // General_Purpose_Register Status_Register: pin names not known; wires that end beside it: or_3_out, Clk, 1'b1, alu_with_controls_1_p21, Status_Register_p5, alu_with_controls_1_p20, Status_Register_p7, alu_with_controls_1_p19, Status_Register_p9, pull_resistor_7_node, Status_Register_p11
  LED led_37 (.in(Status_Register_p7));
  LED led_38 (.in(Status_Register_p5));
  LED led_39 (.in(Status_Register_p9));
  LED led_40 (.in(Status_Register_p11));

  // Notes on the sheet:
  //   R1
  //   R3
  //   R2
  //   R4
  //   Status Register
  //   Z
  //   N
  //   C
endmodule
