// Logisim project General Purpose Register.circ as structural Verilog: 1 circuit, main circuit General Purpose Register
module General_Purpose_Register (
  input  in_1,
  input  in_2,
  input  in_3,
  input  in_4,
  input  in_5,
  input  in_6,
  input  in_7,
  output out_8,
  output out_9,
  output out_10,
  output out_11,
  output out_12,
  output out_13,
  output out_14,
  output out_15
);

  wire controlled_buffer_1_out, controlled_buffer_4_out, controlled_buffer_7_out, controlled_buffer_10_out,
       not_1_out;

  not not_1 (not_1_out, in_5);
  assign controlled_buffer_1_out = in_5 ? in_1 : 1'bz;  // Controlled_Buffer controlled_buffer_1
  assign controlled_buffer_1_out = not_1_out ? out_8 : 1'bz;  // Controlled_Buffer controlled_buffer_2
  D_Flip_Flop d_ff_1 (.clk(in_6), .D(controlled_buffer_1_out), .Q(out_8));  // open: Qn, preset, en, reset
  assign out_12 = in_7 ? out_8 : 1'bz;  // Controlled_Buffer controlled_buffer_3
  assign controlled_buffer_4_out = in_5 ? in_2 : 1'bz;  // Controlled_Buffer controlled_buffer_4
  assign controlled_buffer_4_out = not_1_out ? out_9 : 1'bz;  // Controlled_Buffer controlled_buffer_5
  D_Flip_Flop d_ff_2 (.clk(in_6), .D(controlled_buffer_4_out), .Q(out_9));  // open: Qn, preset, en, reset
  assign out_13 = in_7 ? out_9 : 1'bz;  // Controlled_Buffer controlled_buffer_6
  assign controlled_buffer_7_out = in_5 ? in_3 : 1'bz;  // Controlled_Buffer controlled_buffer_7
  assign controlled_buffer_7_out = not_1_out ? out_10 : 1'bz;  // Controlled_Buffer controlled_buffer_8
  D_Flip_Flop d_ff_3 (.clk(in_6), .D(controlled_buffer_7_out), .Q(out_10));  // open: Qn, preset, en, reset
  assign out_14 = in_7 ? out_10 : 1'bz;  // Controlled_Buffer controlled_buffer_9
  assign controlled_buffer_10_out = in_5 ? in_4 : 1'bz;  // Controlled_Buffer controlled_buffer_10
  assign controlled_buffer_10_out = not_1_out ? out_11 : 1'bz;  // Controlled_Buffer controlled_buffer_11
  D_Flip_Flop d_ff_4 (.clk(in_6), .D(controlled_buffer_10_out), .Q(out_11));  // open: Qn, preset, en, reset
  assign out_15 = in_7 ? out_11 : 1'bz;  // Controlled_Buffer controlled_buffer_12
endmodule
