// Logisim project Instruction Register.circ as structural Verilog: 1 circuit, main circuit Instruction Register
module Instruction_Register (
  input  in_1,
  input  in_2,
  input  in_3,
  input  in_4,
  input  in_5,
  input  in_6,
  input  in_7,
  input  in_8,
  output out_9,
  output out_10,
  output out_11,
  output out_12,
  output out_13,
  output out_14,
  output out_15,
  output out_16,
  output out_17,
  output out_18,
  output out_19,
  output out_20
);

  // General_Purpose_Register general_purpose_register_1: pin names not known; wires that end beside it: in_5, in_7, 1'b1, in_1, out_13, in_2, out_14, in_3, out_15, in_4, out_16
  // General_Purpose_Register general_purpose_register_2: pin names not known; wires that end beside it: in_6, in_7, 1'b1, in_1, out_17, in_2, out_18, in_3, out_19, in_4, out_20
  assign out_9 = in_8 ? out_17 : 1'bz;  // Controlled_Buffer controlled_buffer_1
  assign out_10 = in_8 ? out_18 : 1'bz;  // Controlled_Buffer controlled_buffer_2
  assign out_11 = in_8 ? out_19 : 1'bz;  // Controlled_Buffer controlled_buffer_3
  assign out_12 = in_8 ? out_20 : 1'bz;  // Controlled_Buffer controlled_buffer_4
endmodule
