// Logisim project RAM ROM with MAR.circ as structural Verilog: 1 circuit, main circuit RAM ROM with MAR
module RAM_ROM_with_MAR (
  input  in_1,
  input  in_2,
  input  in_3,
  input  in_4,
  input  in_5,
  input  in_6,
  input  [3:0] in_7,
  input  in_8,
  input  in_9,
  input  in_10,
  input  in_11,
  output [3:0] out_12
);

  wire general_purpose_register_1_p5, general_purpose_register_1_p10, general_purpose_register_1_p13,
       general_purpose_register_1_p15, not_1_out;
  wire [3:0] general_purpose_register_1_p14, ram_1_data, rom_1_data, rom_2_data;

  // General_Purpose_Register general_purpose_register_1: pin names not known; wires that end beside it: in_5, in_6, 1'b1, in_4, general_purpose_register_1_p5, general_purpose_register_1_p14[3], in_3, general_purpose_register_1_p14[2], in_2, general_purpose_register_1_p10, general_purpose_register_1_p14[1], in_1, general_purpose_register_1_p13, general_purpose_register_1_p14[0], general_purpose_register_1_p15
  LED led_1 (.in(general_purpose_register_1_p13));
  LED led_2 (.in(general_purpose_register_1_p5));
  LED led_3 (.in(general_purpose_register_1_p10));
  LED led_4 (.in(general_purpose_register_1_p15));
  ROM #(.addrWidth(4), .dataWidth(4)) rom_1 (.addr(general_purpose_register_1_p14), .data(rom_1_data), .sel(in_11));
  ROM #(.addrWidth(4), .dataWidth(4)) rom_2 (.addr(general_purpose_register_1_p14), .data(rom_2_data), .sel(in_10));
  RAM #(.addrWidth(4), .dataWidth(4)) ram_1 (
    .addr(general_purpose_register_1_p14), .data(ram_1_data), .sel(in_8), .clk(in_6), .ld(in_9), .clr(1'b0));
  assign out_12 = in_11 ? rom_1_data : 4'bz;  // Controlled_Buffer controlled_buffer_1
  assign out_12 = in_10 ? rom_2_data : 4'bz;  // Controlled_Buffer controlled_buffer_2
  assign out_12 = in_9 ? ram_1_data : 4'bz;  // Controlled_Buffer controlled_buffer_3
  assign ram_1_data = not_1_out ? in_7 : 4'bz;  // Controlled_Buffer controlled_buffer_4
  not not_1 (not_1_out, in_9);

  // Notes on the sheet:
  //   ROM 2
  //   ROM 1
  //   RAM
  //   contents of rom_1 (hex, n*v repeats v):
  //   f 0 f
  //   contents of rom_2 (hex, n*v repeats v):
  //   f 0 f
endmodule
